// Logisim project Processador.circ as structural Verilog: 4 circuits, main circuit main
module main (
  input  _13_CLK,
  input  _12_WR1,
  input  _11_WR0,
  input  _6_MR,
  input  _5_S3,
  input  _4_S2,
  input  _3_S1,
  input  _2_S0,
  input  A1_M,
  input  A0_Cin,
  input  _10_RB1,
  input  _9_RB0,
  input  _8_RA1,
  input  _7_RA0,
  output Y3,
  output Y2,
  output Y1,
  output YO,
  output out_19,
  output out_20
);

  wire n7432_1_out_9, n7432_1_out_10, n7432_1_out_11, n7432_1_out_12, n74181_1_p1, n74181_1_p4, n74181_1_p5,
       n74181_1_p6, not_1_out, R3_0_q, R3_1_q, R3_2_q, R3_3_q, undriven, undriven_2, undriven_3, undriven_4;

  D_Flip_Flop R0_3 (.clk(undriven), .D(Y3), .en(1'b1));  // open: Q, Qn, preset, reset
  D_Flip_Flop R1_3 (.clk(undriven_2), .D(Y3), .en(1'b1));  // open: Q, Qn, preset, reset
  D_Flip_Flop R2_3 (.clk(undriven_3), .D(Y3), .en(1'b1));  // open: Q, Qn, preset, reset
  D_Flip_Flop R3_3 (.clk(undriven_4), .D(Y3), .Q(R3_3_q), .en(1'b1));  // open: Qn, preset, reset
  D_Flip_Flop R0_2 (.clk(undriven), .D(Y2), .en(1'b1));  // open: Q, Qn, preset, reset
  D_Flip_Flop R1_2 (.clk(undriven_2), .D(Y2), .en(1'b1));  // open: Q, Qn, preset, reset
  D_Flip_Flop R2_2 (.clk(undriven_3), .D(Y2), .en(1'b1));  // open: Q, Qn, preset, reset
  D_Flip_Flop R3_2 (.clk(undriven_4), .D(Y2), .Q(R3_2_q), .en(1'b1));  // open: Qn, preset, reset
  D_Flip_Flop R0_1 (.clk(undriven), .D(Y1), .en(1'b1));  // open: Q, Qn, preset, reset
  D_Flip_Flop R1_1 (.clk(undriven_2), .D(Y1), .en(1'b1));  // open: Q, Qn, preset, reset
  D_Flip_Flop R2_1 (.clk(undriven_3), .D(Y1), .en(1'b1));  // open: Q, Qn, preset, reset
  D_Flip_Flop R3_1 (.clk(undriven_4), .D(Y1), .Q(R3_1_q), .en(1'b1));  // open: Qn, preset, reset
  D_Flip_Flop R0_0 (.clk(undriven), .D(YO), .en(1'b1));  // open: Q, Qn, preset, reset
  D_Flip_Flop R1_0 (.clk(undriven_2), .D(YO), .en(1'b1));  // open: Q, Qn, preset, reset
  D_Flip_Flop R2_0 (.clk(undriven_3), .D(YO), .en(1'b1));  // open: Q, Qn, preset, reset
  D_Flip_Flop R3_0 (.clk(undriven_4), .D(YO), .Q(R3_0_q), .en(1'b1));  // open: Qn, preset, reset
  _74157 u_74157_1 (
    .Y2(Y2), .B2(n7432_1_out_9), .A2(n74181_1_p4), .Y3(Y3), .B3(n7432_1_out_11), .A3(n74181_1_p1),
    .E_prime(1'b0), .Y1(Y1), .B1(n7432_1_out_12), .A1(n74181_1_p5), .Y0(YO), .B0(n7432_1_out_10),
    .A0(n74181_1_p6), .S(_6_MR));
  // _74181 74181_1: pin names not known; wires that end beside it: n74181_1_p1, out_20, out_19, n74181_1_p4, n74181_1_p5, n74181_1_p6, A1_M, A0_Cin, _2_S0, _3_S1, _4_S2, _5_S3, _12_WR1, _11_WR0
  _7432 u_7432_1 (
    .out_9(n7432_1_out_9), .in_1(not_1_out), .in_3(_8_RA1), .out_11(n7432_1_out_11), .in_5(not_1_out),
    .in_7(_7_RA0), .out_10(n7432_1_out_10), .in_2(not_1_out), .in_4(_10_RB1), .out_12(n7432_1_out_12),
    .in_6(not_1_out), .in_8(_9_RB0));
  _7432 u_7432_2 (
    .in_1(_6_MR), .in_3(_8_RA1), .in_5(_6_MR), .in_7(_7_RA0), .in_2(_6_MR), .in_4(_10_RB1), .in_6(_6_MR),
    .in_8(_9_RB0));  // open: out_9, out_11, out_10, out_12
  not not_1 (not_1_out, _6_MR);

  // Notes on the sheet:
  //   S0
  //   S1
  //   S2
  //   S3
endmodule

module _74157 (
  input  B2,
  input  B1,
  input  A2,
  input  A1,
  input  B3,
  input  B0,
  input  A3,
  input  A0,
  input  S,
  input  E_prime,
  output Y2,
  output Y1,
  output Y3,
  output Y0
);

  wire not_1_out;

  not not_1 (not_1_out, E_prime);
  Multiplexer multiplexer_1 (.in0(B2), .in1(A2), .out(Y2), .sel(S), .en(not_1_out));
  Multiplexer multiplexer_2 (.in0(B1), .in1(A1), .out(Y1), .sel(S), .en(not_1_out));
  Multiplexer multiplexer_3 (.in0(B3), .in1(A3), .out(Y3), .sel(S), .en(not_1_out));
  Multiplexer multiplexer_4 (.in0(B0), .in1(A0), .out(Y0), .sel(S), .en(not_1_out));
endmodule

module _7432 (
  input  in_1,
  input  in_2,
  input  in_3,
  input  in_4,
  input  in_5,
  input  in_6,
  input  in_7,
  input  in_8,
  output out_9,
  output out_10,
  output out_11,
  output out_12
);

  or or_1 (out_9, in_1, in_3);
  or or_2 (out_10, in_2, in_4);
  or or_3 (out_12, in_6, in_8);
  or or_4 (out_11, in_5, in_7);
endmodule

module _74174 (
  input  D3,
  input  D2,
  input  D0,
  input  D1,
  output Q3,
  output Q2,
  output Q0,
  output Q1
);

  D_Flip_Flop R3_2 ();  // open: clk, D, Q, Qn, preset, en, reset
  D_Flip_Flop R3_3 ();  // open: clk, D, Q, Qn, preset, en, reset
  D_Flip_Flop R3_1 (.D(D0));  // open: clk, Q, Qn, preset, en, reset
  // D_Flip_Flop R3_0: pin names not known; wires that end beside it: D1, Q1
endmodule
